// Logisim project not_gate.circ as structural Verilog
module main (
  input  in_1,
  output out_2
);

  test test_1 (.a(in_1), .y(out_2));
endmodule

// VHDL entity test, as the project stores it:
LIBRARY ieee;
USE ieee.std_logic_1164.all;

ENTITY test IS
    PORT (
        a : IN std_logic;
        y : OUT std_logic
    );
END test;

ARCHITECTURE TypeArchitecture OF test IS
BEGIN

    y <= NOT a;

END TypeArchitecture;
